# Fritzing sketch RGB_TEMP (saved by Fritzing 0.9.3b)
breadboards: 1

parts:
  Часть1 = Arduino Uno (Rev3)
  LED1 = RGB LED (com. cathode, rgb) [package="5 mm [THT]"]
  T1 = LM35 Temperature Sensor [package="TO92 [THT]"]
  R1 = Resistor [tolerance=±5% resistance=220 package=THT]
  R2 = Resistor [tolerance=±5% resistance=220 package=THT]
  R3 = Resistor [tolerance=±5% resistance=220 package=THT]

nets (from the breadboard view):
  N1: Часть1.A0, T1.Vout
  N2: Часть1.D9_PWM, R3.Pin_1
  N3: Часть1.D10_PWM/SS, R1.Pin_1
  N4: Часть1.D11_PWM/MOSI, R2.Pin_1
  GND: Часть1.GND, T1.GND
  N5: Часть1.5V, T1.+Vs
  N6: Часть1.VIN, LED1.common_cathode
  N7: LED1.red_anode, R2.Pin_0
  N8: LED1.green_anode, R1.Pin_0
  N9: LED1.blue_anode, R3.Pin_0

// code stored in the sketch: RGM_TEMP.ino
#define tempPin A0;
int redPin = 11;
int greenPin = 10;
int bluePin = 9;
int temp = 0;

void setColor(int red, int green, int blue) {
#ifdef COMMON_ANODE
  red = 255 - red;
  green = 255 - green;
  blue = 255 - blue;
#endif
  analogWrite(redPin, red);
  analogWrite(greenPin, green);
  analogWrite(bluePin, blue);
}

void setup() {
  Serial.begin(9600);
  pinMode(redPin, OUTPUT);
  pinMode(greenPin, OUTPUT);
  pinMode(bluePin, OUTPUT);
}

void loop() {
  int reading = analogRead(A0);
  float voltage = reading * 5.0;
  voltage /= 1024.0;
  float temperatuteC = voltage * 100;
  Serial.print(temperatuteC); Serial.println(" degrees C");

  if (temperatuteC <= 0.0) setColor(0, 100, 255);
  if (temperatuteC > 0.0 && temperatuteC < 17.0) setColor(255, 184, 0);
  if (temperatuteC > 17.0 && temperatuteC <= 20.0) setColor(255, 255, 0);
  if (temperatuteC > 20.0) setColor(255, 50, 0);
  delay(500);
}
